# Fritzing sketch group (saved by Fritzing 0.9.3b)
breadboards: 2

parts:
  Arduino_Uno = Arduino Uno (Rev3)
  Raspberry_Pi_1 = Raspberry Pi 3 [part_number=RPI-3-V1.2]
  R1 = Resistor [tolerance=±5% resistance=3.3k package=THT]
  R2 = Resistor [tolerance=±5% resistance=1.5k package=THT]
  R3 = Resistor [tolerance=±5% resistance=100 package=THT]
  S1 = Pushbutton [package="[THT]"]
  R4 = Resistor [tolerance=±5% resistance=10k package=THT]

nets:
  GND: Arduino_Uno.GND, Raspberry_Pi_1.GND, R1.Pin_0, R4.Pin_1
  N1: Arduino_Uno.D0/RX, Raspberry_Pi_1.GIPO14
  N2: Arduino_Uno.D1/TX, R2.Pin_0
  N3: Arduino_Uno.D2, S1.Pin_1, S1.Pin_2, R4.Pin_0
  N4: Arduino_Uno.5V, S1.Pin_3, S1.Pin_4
  N5: Raspberry_Pi_1.GIPO15, R1.Pin_1, R3.Pin_1
  N6: R2.Pin_1, R3.Pin_0
